# Fritzing sketch pcb_schema (saved by Fritzing 0.9.10b)
circuit board: 3.9cm x 7.6cm
breadboards: 2

parts:
  IN12A1 = IN12A [part_number=IN12A]
  IC1 = MCP23017 I2C I/O Expander
  J1 = male pin header, 3 pins [form="♂ (male)"]
  J3 = male pin header, 3 pins [form="♂ (male)"]
  R7 = Resistor [tolerance=±5% resistance=15k power=0.25 package=THT]
  R6 = Resistor [tolerance=±5% resistance=15k power=0.25 package=THT]
  R5 = Resistor [tolerance=±5% resistance=15k power=0.25 package=THT]
  R4 = Resistor [tolerance=±5% resistance=15k power=0.25 package=THT]
  R3 = Resistor [tolerance=±5% resistance=15k power=0.25 package=THT]
  R2 = Resistor [tolerance=±5% resistance=15k power=0.25 package=THT]
  R8 = Resistor [tolerance=±5% resistance=15k power=0.25 package=THT]
  R9 = Resistor [tolerance=±5% resistance=15k power=0.25 package=THT]
  R0 = Resistor [tolerance=±5% resistance=15k power=0.25 package=THT]
  R1 = Resistor [tolerance=±5% resistance=15k power=0.25 package=THT]
  RNC = Resistor [tolerance=±5% resistance=15k power=0.25 package=THT]
  R12 = Resistor [tolerance=±5% resistance=22000 power=0.25 package=THT]
  J2 = male pin header, 3 pins [form="♂ (male)"]
  MSPA51 = TRANSISTOR_NPN [package=to-92]
  MSPA50 = TRANSISTOR_NPN [package=to-92]
  MSPA49 = TRANSISTOR_NPN [package=to-92]
  MSPA48 = TRANSISTOR_NPN [package=to-92]
  MSPA43 = TRANSISTOR_NPN [package=to-92]
  MSPA44 = TRANSISTOR_NPN [package=to-92]
  MSPA42 = TRANSISTOR_NPN [package=to-92]
  MSPA46 = TRANSISTOR_NPN [package=to-92]
  MSPA47 = TRANSISTOR_NPN [package=to-92]
  MSPA52 = TRANSISTOR_NPN [package=to-92]
  MSPA45 = TRANSISTOR_NPN [package=to-92]
  J6 = male pin header, 4 pins [form="♂ (male)"]
  J7 = male pin header, 4 pins [form="♂ (male)"]
  J8 = Screw terminal - 2 pins [package=THT]

nets:
  N1: IN12A1.pin1, MSPA43.C
  N2: IN12A1.pin2, MSPA44.C
  N3: IN12A1.pin3, MSPA42.C
  N4: IN12A1.pin4, MSPA46.C
  N5: IN12A1.pin5, MSPA47.C
  N6: IN12A1.pin6, MSPA52.C
  N7: IN12A1.pin7, MSPA45.C
  N8: IN12A1.pin8, MSPA51.C
  N9: IN12A1.pin9, MSPA50.C
  N10: IN12A1.pin0, MSPA49.C
  N11: IN12A1.pinAnode, R12.Pin_1
  N12: IN12A1.pinNC, MSPA48.C
  N13: IC1.GPB0, R2.Pin_1
  N14: IC1.GPB1, R3.Pin_1
  N15: IC1.GPB2, R4.Pin_1
  N16: IC1.VDD, IC1.RESET, J1.pin3, J3.pin3, J2.pin3, J6.pin3, J7.pin2
  N17: IC1.VSS, J1.pin1, J3.pin1, J2.pin1, J6.pin4, J7.pin1
  N18: IC1.SCL, J6.pin1, J7.pin4
  N19: IC1.SDA, J6.pin2, J7.pin3
  N20: IC1.A0, J1.pin2
  N21: IC1.A1, J2.pin2
  N22: IC1.A2, J3.pin2
  N23: IC1.GPA0, R0.Pin_1
  N24: IC1.GPA1, R9.Pin_1
  N25: IC1.GPA2, R8.Pin_1
  N26: IC1.GPA3, R7.Pin_1
  N27: IC1.GPA4, R6.Pin_1
  N28: IC1.GPA5, RNC.Pin_1
  N29: IC1.GPA6, R5.Pin_1
  N30: IC1.GPA7, R1.Pin_1
  N31: R7.Pin_0, MSPA45.B
  N32: R6.Pin_0, MSPA52.B
  N33: R5.Pin_0, MSPA47.B
  N34: R4.Pin_0, MSPA46.B
  N35: R3.Pin_0, MSPA42.B
  N36: R2.Pin_0, MSPA44.B
  N37: R8.Pin_0, MSPA51.B
  N38: R9.Pin_0, MSPA50.B
  N39: R0.Pin_0, MSPA49.B
  N40: R1.Pin_0, MSPA43.B
  N41: RNC.Pin_0, MSPA48.B
  N42: R12.Pin_0, J8.pin1
  N43: MSPA51.E, MSPA50.E, MSPA49.E, MSPA48.E, MSPA43.E, MSPA44.E, MSPA42.E, MSPA46.E, MSPA47.E, MSPA52.E, MSPA45.E, J8.pin2

custom parts:
  IN12A: A 12pin IN12A Nixie Tube
  MCP23017 I2C I/O Expander: The MCP23017 uses two i2c pins (these can be shared with other i2c devices), and in exchange gives you 16 general purpose pins. You can set each of 16 pins to be input, output, input with a pullup or open drain. There's even the ability to get an interrupt via an external pin when any of the inputs change so you don't have to keep polling the chip.
